// Logisim project main.circ as structural Verilog: 8 circuits, main circuit main
module main (
);

  wire button_1_out, button_2_out, button_3_out, stage1_1_output1, stage2_1_op1, stage2_1_op2, stage2_1_op3,
       stage2_1_op4, stage2_1_ouput5, stage3_1_op5, stage3_1_op6, stage3_1_op7, stage3_1_op8,
       stage3_1_output5, stage4_2_1_op9, stage4_2_1_op10, stage4_2_1_op11, stage4_2_1_op12, stage4_2_1_op13,
       stage4_2_1_op14, stage4_2_1_op15, stage4_2_1_op16;
  wire [3:0] stage2_1_hexlightsec, stage3_1_hexlightsec, stage4_2_1_out_8, stage4_2_1_out_13,
       stage5_1_lighmin1, stage5_1_lighsec1, stage5_1_lightmin2, stage5_1_lightsec2;

  stage5 stage5_1 (
    .reset(button_3_out), .split(button_2_out), .pin1(stage2_1_op1), .pin2(stage2_1_op2),
    .pin3(stage2_1_op3), .pin4(stage2_1_op4), .pin5(stage3_1_op5), .pin6(stage3_1_op6), .pin7(stage3_1_op8),
    .pin8(stage3_1_op7), .pin9(stage4_2_1_op9), .pin10(stage4_2_1_op10), .pin11(stage4_2_1_op11),
    .pin12(stage4_2_1_op12), .pin13(stage4_2_1_op13), .pin14(stage4_2_1_op14), .pin15(stage4_2_1_op15),
    .pin16(stage4_2_1_op16), .lighmin1(stage5_1_lighmin1), .lightmin2(stage5_1_lightmin2),
    .lighsec1(stage5_1_lighsec1), .lightsec2(stage5_1_lightsec2));
  Button button_1 (.out(button_1_out));
  Hex_Digit_Display hex_digit_display_1 (.value(stage4_2_1_out_13));  // open: dp
  Button button_2 (.out(button_2_out));
  Hex_Digit_Display hex_digit_display_2 (.value(stage4_2_1_out_8));  // open: dp
  Button button_3 (.out(button_3_out));
  Hex_Digit_Display hex_digit_display_3 (.value(stage3_1_hexlightsec));  // open: dp
  Hex_Digit_Display hex_digit_display_4 (.value(stage2_1_hexlightsec));  // open: dp
  Hex_Digit_Display hex_digit_display_5 (.value(stage5_1_lighmin1));  // open: dp
  stage1 stage1_1 (.start(button_1_out), .reset(button_3_out), .output1(stage1_1_output1));
  Hex_Digit_Display hex_digit_display_6 (.value(stage5_1_lightmin2));  // open: dp
  LED led_1 (.in(stage1_1_output1));
  Hex_Digit_Display hex_digit_display_7 (.value(stage5_1_lighsec1));  // open: dp
  Hex_Digit_Display hex_digit_display_8 (.value(stage5_1_lightsec2));  // open: dp
  stage4_2 stage4_2_1 (
    .start(stage1_1_output1), .reset(button_3_out), .output5(stage3_1_output5), .op9(stage4_2_1_op9),
    .op10(stage4_2_1_op10), .op11(stage4_2_1_op11), .op12(stage4_2_1_op12), .out_8(stage4_2_1_out_8),
    .op13(stage4_2_1_op13), .op14(stage4_2_1_op14), .op15(stage4_2_1_op15), .op16(stage4_2_1_op16),
    .out_13(stage4_2_1_out_13));
  stage2 stage2_1 (
    .start(stage1_1_output1), .reset(button_3_out), .op1(stage2_1_op1), .op2(stage2_1_op2),
    .op3(stage2_1_op3), .op4(stage2_1_op4), .hexlightsec(stage2_1_hexlightsec), .ouput5(stage2_1_ouput5));
  stage3 stage3_1 (
    .start(stage1_1_output1), .reset(button_3_out), .input5(stage2_1_ouput5),
    .hexlightsec(stage3_1_hexlightsec), .op5(stage3_1_op5), .op6(stage3_1_op6), .op7(stage3_1_op7),
    .op8(stage3_1_op8), .output5(stage3_1_output5));

  // Notes on the sheet:
  //   Tran Quang Huy 
  //   Studentid: 106212636
  //   Start / Stop
  //   Minutes
  //   Split
  //   Elapsed Time
  //   :
  //   Reset
  //   Seconds
  //   Stopwatch Interface
  //   Split Time
  //   Minutes
  //   Clock Started
  //   Seconds
  //   :
endmodule

module stage1 (
  input  start,
  input  reset,
  output output1
);

  J_K_Flip_Flop j_k_ff_1 (.J(start), .K(start), .clk(start), .Q(output1), .reset(reset));  // open: Qn, preset
  LED led_1 (.in(output1));

  // Notes on the sheet:
  //   Start / Stop
  //   Reset
  //   Clock Started
  //   Sending signal to other stage
endmodule

module stage2 (
  input  start,
  input  reset,
  output op1,
  output op2,
  output op3,
  output op4,
  output [3:0] hexlightsec,
  output ouput5
);

  wire clock_1_out, or_1_out;

  Clock clock_1 (.out(clock_1_out));
  J_K_Flip_Flop #(.trigger("falling")) j_k_ff_1 (
    .J(start), .K(start), .clk(clock_1_out), .Q(hexlightsec[0]), .reset(or_1_out));  // open: Qn, preset
  or or_1 (or_1_out, reset, ouput5);
  J_K_Flip_Flop #(.trigger("falling")) j_k_ff_2 (
    .J(start), .K(start), .clk(hexlightsec[0]), .Q(hexlightsec[1]), .reset(or_1_out));  // open: Qn, preset
  J_K_Flip_Flop #(.trigger("falling")) j_k_ff_3 (
    .J(start), .K(start), .clk(hexlightsec[1]), .Q(hexlightsec[2]), .reset(or_1_out));  // open: Qn, preset
  LED led_1 (.in(start));
  J_K_Flip_Flop #(.trigger("falling")) j_k_ff_4 (
    .J(start), .K(start), .clk(hexlightsec[2]), .Q(hexlightsec[3]), .reset(or_1_out));  // open: Qn, preset
  and and_1 (ouput5, hexlightsec[1], hexlightsec[3]);

  assign op1 = hexlightsec[0];
  assign op2 = hexlightsec[1];
  assign op3 = hexlightsec[2];
  assign op4 = hexlightsec[3];

  // Notes on the sheet:
  //   Start / Stop
  //   Reset
  //   Clock Started
endmodule

module stage3 (
  input  start,
  input  reset,
  input  input5,
  output [3:0] hexlightsec,
  output op5,
  output op6,
  output op7,
  output op8,
  output output5
);

  wire not_1_out, or_1_out;

  J_K_Flip_Flop #(.trigger("falling")) j_k_ff_1 (
    .J(start), .K(start), .clk(input5), .Q(hexlightsec[0]), .reset(or_1_out));  // open: Qn, preset
  or or_1 (or_1_out, reset, output5);
  not not_1 (not_1_out, hexlightsec[0]);
  LED led_1 (.in(start));
  J_K_Flip_Flop #(.trigger("falling")) j_k_ff_2 (
    .J(start), .K(start), .clk(hexlightsec[0]), .Q(hexlightsec[1]), .reset(or_1_out));  // open: Qn, preset
  and and_1 (output5, not_1_out, hexlightsec[1], hexlightsec[2]);
  J_K_Flip_Flop #(.trigger("falling")) j_k_ff_3 (
    .J(start), .K(start), .clk(hexlightsec[1]), .Q(hexlightsec[2]), .reset(or_1_out));  // open: Qn, preset
  Hex_Digit_Display hex_digit_display_1 (.value({1'b0, hexlightsec[2:0]}));  // open: dp

  assign hexlightsec[3] = 1'b0;
  assign op5 = hexlightsec[0];
  assign op6 = hexlightsec[1];
  assign op7 = hexlightsec[2];
  assign op8 = 1'b0;

  // Notes on the sheet:
  //   Start / Stop
  //   Reset
  //   Clock Started
endmodule

module stage4 (
  input  start,
  input  reset,
  input  output5,
  output [3:0] out_4,
  output [3:0] out_5
);

  wire and_1_out, and_2_out, or_1_out, or_2_out;

  J_K_Flip_Flop #(.trigger("falling")) j_k_ff_1 (
    .J(start), .K(start), .clk(output5), .Q(out_5[0]), .reset(or_1_out));  // open: Qn, preset
  J_K_Flip_Flop #(.trigger("falling")) j_k_ff_2 (
    .J(start), .K(start), .clk(and_1_out), .Q(out_4[0]), .preset(or_2_out));  // open: Qn, reset
  or or_1 (or_1_out, reset, and_1_out);
  or or_2 (or_2_out, reset, and_2_out);
  J_K_Flip_Flop #(.trigger("falling")) j_k_ff_3 (
    .J(start), .K(start), .clk(out_5[0]), .Q(out_5[1]), .preset(reset), .reset(and_1_out));  // open: Qn
  J_K_Flip_Flop #(.trigger("falling")) j_k_ff_4 (
    .J(start), .K(start), .clk(out_4[0]), .Q(out_4[1]), .preset(or_2_out));  // open: Qn, reset
  LED led_1 (.in(start));
  J_K_Flip_Flop #(.trigger("falling")) j_k_ff_5 (
    .J(start), .K(start), .clk(out_5[1]), .Q(out_5[2]), .preset(reset), .reset(and_1_out));  // open: Qn
  J_K_Flip_Flop #(.trigger("falling")) j_k_ff_6 (
    .J(start), .K(start), .clk(out_4[1]), .Q(out_4[2]), .reset(or_2_out));  // open: Qn, preset
  J_K_Flip_Flop #(.trigger("falling")) j_k_ff_7 (
    .J(start), .K(start), .clk(out_5[2]), .Q(out_5[3]), .reset(or_1_out));  // open: Qn, preset
  and and_1 (and_1_out, out_5[1], out_5[3]);
  J_K_Flip_Flop #(.trigger("falling")) j_k_ff_8 (
    .J(start), .K(start), .clk(out_4[2]), .Q(out_4[3]), .reset(or_2_out));  // open: Qn, preset
  and and_2 (and_2_out, out_4[1], out_4[3]);
  Hex_Digit_Display hex_digit_display_1 (.value(out_4));  // open: dp
  Hex_Digit_Display hex_digit_display_2 (.value(out_5));  // open: dp

  // Notes on the sheet:
  //   Start / Stop
  //   Reset
endmodule

module stage4_2 (
  input  start,
  input  reset,
  input  output5,
  output op9,
  output op10,
  output op11,
  output op12,
  output [3:0] out_8,
  output op13,
  output op14,
  output op15,
  output op16,
  output [3:0] out_13
);

  wire and_1_out, and_2_out, and_3_out, nand_1_out, or_1_out, or_2_out;

  and and_1 (and_1_out, nand_1_out, start);
  J_K_Flip_Flop #(.trigger("falling")) j_k_ff_1 (
    .J(and_1_out), .K(and_1_out), .clk(output5), .Q(op9), .reset(or_1_out));  // open: Qn, preset
  J_K_Flip_Flop #(.trigger("falling")) j_k_ff_2 (
    .J(and_1_out), .K(and_1_out), .clk(and_2_out), .Q(op13), .preset(or_2_out));  // open: Qn, reset
  or or_1 (or_1_out, reset, and_2_out);
  or or_2 (or_2_out, reset, and_3_out);
  J_K_Flip_Flop #(.trigger("falling")) j_k_ff_3 (
    .J(and_1_out), .K(and_1_out), .clk(op9), .Q(op10), .preset(reset), .reset(and_2_out));  // open: Qn
  J_K_Flip_Flop #(.trigger("falling")) j_k_ff_4 (
    .J(and_1_out), .K(and_1_out), .clk(op13), .Q(op14), .preset(or_2_out));  // open: Qn, reset
  J_K_Flip_Flop #(.trigger("falling")) j_k_ff_5 (
    .J(and_1_out), .K(and_1_out), .clk(op10), .Q(op11), .preset(reset), .reset(and_2_out));  // open: Qn
  J_K_Flip_Flop #(.trigger("falling")) j_k_ff_6 (
    .J(and_1_out), .K(and_1_out), .clk(op14), .Q(op15), .reset(or_2_out));  // open: Qn, preset
  J_K_Flip_Flop #(.trigger("falling")) j_k_ff_7 (
    .J(and_1_out), .K(and_1_out), .clk(op11), .Q(op12), .reset(or_1_out));  // open: Qn, preset
  and and_2 (and_2_out, op10, op12);
  J_K_Flip_Flop #(.trigger("falling")) j_k_ff_8 (
    .J(and_1_out), .K(and_1_out), .clk(op15), .Q(op16), .reset(or_2_out));  // open: Qn, preset
  and and_3 (and_3_out, op14, op16);
  Hex_Digit_Display hex_digit_display_1 (.value({op12, op11, op10, op9}));  // open: dp
  Hex_Digit_Display hex_digit_display_2 (.value({op16, op15, op14, op13}));  // open: dp
  nand nand_1 (nand_1_out, op12, op9, op13, op16);

  assign out_8 = {op12, op11, op10, op9};
  assign out_13 = {op16, op15, op14, op13};
endmodule

module stage5 (
  input  reset,
  input  split,
  input  pin1,
  input  pin2,
  input  pin3,
  input  pin4,
  input  pin5,
  input  pin6,
  input  pin7,
  input  pin8,
  input  pin9,
  input  pin10,
  input  pin11,
  input  pin12,
  input  pin13,
  input  pin14,
  input  pin15,
  input  pin16,
  output [3:0] lighmin1,
  output [3:0] lightmin2,
  output [3:0] lighsec1,
  output [3:0] lightsec2
);

  wire split_counter_1_clock;

  split_counter split_counter_1 (.split(split), .reset(reset), .clock(split_counter_1_clock));
  D_Flip_Flop d_ff_1 (.D(pin1), .clk(split_counter_1_clock), .Q(lightsec2[0]), .reset(reset));  // open: Qn, preset
  D_Flip_Flop d_ff_2 (.D(pin2), .clk(split_counter_1_clock), .Q(lightsec2[1]), .reset(reset));  // open: Qn, preset
  D_Flip_Flop d_ff_3 (.D(pin3), .clk(split_counter_1_clock), .Q(lightsec2[2]), .reset(reset));  // open: Qn, preset
  D_Flip_Flop d_ff_4 (.D(pin4), .clk(split_counter_1_clock), .Q(lightsec2[3]), .reset(reset));  // open: Qn, preset
  D_Flip_Flop d_ff_5 (.D(pin5), .clk(split_counter_1_clock), .Q(lighsec1[0]), .reset(reset));  // open: Qn, preset
  D_Flip_Flop d_ff_6 (.D(pin6), .clk(split_counter_1_clock), .Q(lighsec1[1]), .reset(reset));  // open: Qn, preset
  D_Flip_Flop d_ff_7 (.D(pin7), .clk(split_counter_1_clock), .Q(lighsec1[2]), .reset(reset));  // open: Qn, preset
  D_Flip_Flop d_ff_8 (.D(pin8), .clk(split_counter_1_clock), .Q(lighsec1[3]), .reset(reset));  // open: Qn, preset
  D_Flip_Flop d_ff_9 (.D(pin9), .clk(split_counter_1_clock), .Q(lightmin2[0]), .reset(reset));  // open: Qn, preset
  D_Flip_Flop d_ff_10 (.D(pin10), .clk(split_counter_1_clock), .Q(lightmin2[1]), .preset(reset));  // open: Qn, reset
  D_Flip_Flop d_ff_11 (.D(pin11), .clk(split_counter_1_clock), .Q(lightmin2[2]), .preset(reset));  // open: Qn, reset
  D_Flip_Flop d_ff_12 (.D(pin12), .clk(split_counter_1_clock), .Q(lightmin2[3]), .reset(reset));  // open: Qn, preset
  D_Flip_Flop d_ff_13 (.D(pin13), .clk(split_counter_1_clock), .Q(lighmin1[0]), .preset(reset));  // open: Qn, reset
  D_Flip_Flop d_ff_14 (.D(pin14), .clk(split_counter_1_clock), .Q(lighmin1[1]), .preset(reset));  // open: Qn, reset
  D_Flip_Flop d_ff_15 (.D(pin15), .clk(split_counter_1_clock), .Q(lighmin1[2]), .reset(reset));  // open: Qn, preset
  D_Flip_Flop d_ff_16 (.D(pin16), .clk(split_counter_1_clock), .Q(lighmin1[3]), .reset(reset));  // open: Qn, preset
  Hex_Digit_Display hex_digit_display_1 (.value(lighmin1));  // open: dp
  Hex_Digit_Display hex_digit_display_2 (.value(lightmin2));  // open: dp
  Hex_Digit_Display hex_digit_display_3 (.value(lighsec1));  // open: dp
  Hex_Digit_Display hex_digit_display_4 (.value(lightsec2));  // open: dp

  // Notes on the sheet:
  //   Reset
  //   Minutes
  //   Split Time
  //   :
  //   Seconds
endmodule

module split_counter (
  input  split,
  input  reset,
  output clock
);

  wire and_1_out, and_2_out, j_k_ff_1_q, j_k_ff_2_q, j_k_ff_3_q, not_1_out, not_2_out;

  and and_1 (and_1_out, not_1_out, 1'b1);
  not not_1 (not_1_out, and_2_out);
  J_K_Flip_Flop #(.trigger("falling")) j_k_ff_1 (
    .J(and_1_out), .K(and_1_out), .clk(split), .Q(j_k_ff_1_q), .reset(reset));  // open: Qn, preset
  J_K_Flip_Flop #(.trigger("falling")) j_k_ff_2 (
    .J(and_1_out), .K(and_1_out), .clk(j_k_ff_1_q), .Q(j_k_ff_2_q), .reset(reset));  // open: Qn, preset
  J_K_Flip_Flop #(.trigger("falling")) j_k_ff_3 (
    .J(and_1_out), .K(and_1_out), .clk(j_k_ff_2_q), .Q(j_k_ff_3_q), .reset(reset));  // open: Qn, preset
  and and_2 (and_2_out, j_k_ff_2_q, j_k_ff_3_q);
  not not_2 (not_2_out, and_2_out);
  and and_3 (clock, split, not_2_out);
endmodule
