// Logisim project stage1.circ as structural Verilog: 1 circuit, main circuit main
module main (
  output output1
);

  wire button_1_out, button_2_out;

  Button button_1 (.out(button_1_out));
  Button button_2 (.out(button_2_out));
  J_K_Flip_Flop j_k_ff_1 (
    .J(button_1_out), .K(button_1_out), .clk(button_1_out), .Q(output1), .reset(button_2_out));  // open: Qn, preset
  LED led_1 (.in(output1));

  // Notes on the sheet:
  //   Start / Stop
  //   Reset
  //   Clock Started
  //   Sending signal to other stage
endmodule
