// Logisim project stage2.circ as structural Verilog: 2 circuits, main circuit stage1
module stage1 (
  input  start,
  input  reset,
  output output1
);

  J_K_Flip_Flop j_k_ff_1 (.J(start), .K(start), .clk(start), .Q(output1), .reset(reset));  // open: Qn, preset
  LED led_1 (.in(output1));

  // Notes on the sheet:
  //   Start / Stop
  //   Reset
  //   Clock Started
  //   Sending signal to other stage
endmodule

module stage2 (
  output output1
);

  wire button_1_out, button_2_out, clock_1_out, or_1_out, stage1_1_output1;
  wire [3:0] j_k_ff_1_q;

  Clock clock_1 (.out(clock_1_out));
  Button button_1 (.out(button_1_out));
  J_K_Flip_Flop #(.trigger("falling")) j_k_ff_1 (
    .J(stage1_1_output1), .K(stage1_1_output1), .clk(clock_1_out), .Q(j_k_ff_1_q[0]), .reset(or_1_out));  // open: Qn, preset
  Button button_2 (.out(button_2_out));
  or or_1 (or_1_out, button_2_out, output1);
  J_K_Flip_Flop #(.trigger("falling")) j_k_ff_2 (
    .J(stage1_1_output1), .K(stage1_1_output1), .clk(j_k_ff_1_q[0]), .Q(j_k_ff_1_q[1]), .reset(or_1_out));  // open: Qn, preset
  stage1 stage1_1 (.start(button_1_out), .reset(button_2_out), .output1(stage1_1_output1));
  J_K_Flip_Flop #(.trigger("falling")) j_k_ff_3 (
    .J(stage1_1_output1), .K(stage1_1_output1), .clk(j_k_ff_1_q[1]), .Q(j_k_ff_1_q[2]), .reset(or_1_out));  // open: Qn, preset
  LED led_1 (.in(stage1_1_output1));
  J_K_Flip_Flop #(.trigger("falling")) j_k_ff_4 (
    .J(stage1_1_output1), .K(stage1_1_output1), .clk(j_k_ff_1_q[2]), .Q(j_k_ff_1_q[3]), .reset(or_1_out));  // open: Qn, preset
  and and_1 (output1, j_k_ff_1_q[1], j_k_ff_1_q[3]);
  Hex_Digit_Display hex_digit_display_1 (.value(j_k_ff_1_q));  // open: dp

  // Notes on the sheet:
  //   Start / Stop
  //   Reset
  //   Clock Started
endmodule
