// Logisim project stage3.circ as structural Verilog: 3 circuits, main circuit stage2
module stage1 (
  input  start,
  input  reset,
  output output1
);

  J_K_Flip_Flop j_k_ff_1 (.J(start), .K(start), .clk(start), .Q(output1), .reset(reset));  // open: Qn, preset
  LED led_1 (.in(output1));

  // Notes on the sheet:
  //   Start / Stop
  //   Reset
  //   Clock Started
  //   Sending signal to other stage
endmodule

module stage2 (
  input  InputA,
  input  InputB,
  output [3:0] hexlightsec,
  output ouput1
);

  wire clock_1_out, or_1_out, stage1_1_output1;

  Clock clock_1 (.out(clock_1_out));
  J_K_Flip_Flop #(.trigger("falling")) j_k_ff_1 (
    .J(stage1_1_output1), .K(stage1_1_output1), .clk(clock_1_out), .Q(hexlightsec[0]), .reset(or_1_out));  // open: Qn, preset
  or or_1 (or_1_out, InputB, ouput1);
  J_K_Flip_Flop #(.trigger("falling")) j_k_ff_2 (
    .J(stage1_1_output1), .K(stage1_1_output1), .clk(hexlightsec[0]), .Q(hexlightsec[1]), .reset(or_1_out));  // open: Qn, preset
  stage1 stage1_1 (.start(InputA), .reset(InputB), .output1(stage1_1_output1));
  J_K_Flip_Flop #(.trigger("falling")) j_k_ff_3 (
    .J(stage1_1_output1), .K(stage1_1_output1), .clk(hexlightsec[1]), .Q(hexlightsec[2]), .reset(or_1_out));  // open: Qn, preset
  LED led_1 (.in(stage1_1_output1));
  J_K_Flip_Flop #(.trigger("falling")) j_k_ff_4 (
    .J(stage1_1_output1), .K(stage1_1_output1), .clk(hexlightsec[2]), .Q(hexlightsec[3]), .reset(or_1_out));  // open: Qn, preset
  and and_1 (ouput1, hexlightsec[1], hexlightsec[3]);

  // Notes on the sheet:
  //   Start / Stop
  //   Reset
endmodule

module stage3 (
  input  in_1,
  output out_2
);

  wire button_1_out, button_2_out, not_1_out, or_1_out, stage1_1_output1, stage2_1_ouput1;
  wire [2:0] j_k_ff_1_q;
  wire [3:0] stage2_1_hexlightsec;

  Button button_1 (.out(button_1_out));
  Button button_2 (.out(button_2_out));
  stage1 stage1_1 (.start(button_1_out), .reset(button_2_out), .output1(stage1_1_output1));
  J_K_Flip_Flop #(.trigger("falling")) j_k_ff_1 (
    .J(stage1_1_output1), .K(stage1_1_output1), .clk(stage2_1_ouput1), .Q(j_k_ff_1_q[0]), .reset(or_1_out));  // open: Qn, preset
  or or_1 (or_1_out, button_2_out, out_2);
  LED led_1 (.in(stage1_1_output1));
  not not_1 (not_1_out, j_k_ff_1_q[0]);
  J_K_Flip_Flop #(.trigger("falling")) j_k_ff_2 (
    .J(stage1_1_output1), .K(stage1_1_output1), .clk(j_k_ff_1_q[0]), .Q(j_k_ff_1_q[1]), .reset(or_1_out));  // open: Qn, preset
  and and_1 (out_2, not_1_out, j_k_ff_1_q[1], j_k_ff_1_q[2]);
  stage2 stage2_1 (
    .InputA(stage1_1_output1), .InputB(button_2_out), .hexlightsec(stage2_1_hexlightsec),
    .ouput1(stage2_1_ouput1));
  J_K_Flip_Flop #(.trigger("falling")) j_k_ff_3 (
    .J(stage1_1_output1), .K(stage1_1_output1), .clk(j_k_ff_1_q[1]), .Q(j_k_ff_1_q[2]), .reset(or_1_out));  // open: Qn, preset
  Hex_Digit_Display hex_digit_display_1 (.value({in_1, j_k_ff_1_q}));  // open: dp
  Hex_Digit_Display hex_digit_display_2 (.value(stage2_1_hexlightsec));  // open: dp

  // Notes on the sheet:
  //   Start / Stop
  //   Reset
  //   Clock Started
endmodule
