// Logisim project stage4.circ as structural Verilog: 4 circuits, main circuit stage2
module stage1 (
  input  start,
  input  reset,
  output output1
);

  J_K_Flip_Flop j_k_ff_1 (.J(start), .K(start), .clk(start), .Q(output1), .reset(reset));  // open: Qn, preset
  LED led_1 (.in(output1));

  // Notes on the sheet:
  //   Start / Stop
  //   Reset
  //   Clock Started
  //   Sending signal to other stage
endmodule

module stage2 (
  input  start,
  input  reset,
  output op1,
  output op2,
  output op3,
  output op4,
  output [3:0] hexlightsec,
  output ouput1
);

  wire clock_1_out, or_1_out, stage1_1_output1;

  Clock clock_1 (.out(clock_1_out));
  J_K_Flip_Flop #(.trigger("falling")) j_k_ff_1 (
    .J(stage1_1_output1), .K(stage1_1_output1), .clk(clock_1_out), .Q(hexlightsec[0]), .reset(or_1_out));  // open: Qn, preset
  or or_1 (or_1_out, reset, ouput1);
  J_K_Flip_Flop #(.trigger("falling")) j_k_ff_2 (
    .J(stage1_1_output1), .K(stage1_1_output1), .clk(hexlightsec[0]), .Q(hexlightsec[1]), .reset(or_1_out));  // open: Qn, preset
  J_K_Flip_Flop #(.trigger("falling")) j_k_ff_3 (
    .J(stage1_1_output1), .K(stage1_1_output1), .clk(hexlightsec[1]), .Q(hexlightsec[2]), .reset(or_1_out));  // open: Qn, preset
  stage1 stage1_1 (.start(start), .reset(reset), .output1(stage1_1_output1));
  J_K_Flip_Flop #(.trigger("falling")) j_k_ff_4 (
    .J(stage1_1_output1), .K(stage1_1_output1), .clk(hexlightsec[2]), .Q(hexlightsec[3]), .reset(or_1_out));  // open: Qn, preset
  LED led_1 (.in(stage1_1_output1));
  and and_1 (ouput1, hexlightsec[1], hexlightsec[3]);

  assign op1 = hexlightsec[0];
  assign op2 = hexlightsec[1];
  assign op3 = hexlightsec[2];
  assign op4 = hexlightsec[3];

  // Notes on the sheet:
  //   Start / Stop
  //   Reset
  //   Clock Started
endmodule

module stage3 (
  input  start,
  input  reset,
  input  sig,
  input  consta,
  output [3:0] hexlightmin,
  output op1,
  output op2,
  output op3,
  output op4,
  output output5
);

  wire not_1_out, or_1_out, stage1_1_output1, stage2_1_op2, stage2_1_ouput1;
  wire [3:0] stage2_1_hexlightsec;

  stage1 stage1_1 (.start(start), .reset(reset), .output1(stage1_1_output1));
  J_K_Flip_Flop #(.trigger("falling")) j_k_ff_1 (
    .J(stage1_1_output1), .K(stage1_1_output1), .clk(sig), .Q(hexlightmin[0]), .reset(or_1_out));  // open: Qn, preset
  or or_1 (or_1_out, reset, output5);
  LED led_1 (.in(stage1_1_output1));
  not not_1 (not_1_out, hexlightmin[0]);
  J_K_Flip_Flop #(.trigger("falling")) j_k_ff_2 (
    .J(stage1_1_output1), .K(stage1_1_output1), .clk(hexlightmin[0]), .Q(hexlightmin[1]), .reset(or_1_out));  // open: Qn, preset
  and and_1 (output5, not_1_out, hexlightmin[1], hexlightmin[2]);
  stage2 stage2_1 (
    .start(stage1_1_output1), .reset(reset), .op2(stage2_1_op2), .hexlightsec(stage2_1_hexlightsec),
    .ouput1(stage2_1_ouput1));  // open: op1, op3, op4
  J_K_Flip_Flop #(.trigger("falling")) j_k_ff_3 (
    .J(stage1_1_output1), .K(stage1_1_output1), .clk(hexlightmin[1]), .Q(hexlightmin[2]), .reset(or_1_out));  // open: Qn, preset
  Hex_Digit_Display hex_digit_display_1 (.value(stage2_1_hexlightsec));  // open: dp

  assign hexlightmin[3] = consta;
  assign op1 = hexlightmin[0];
  assign op2 = hexlightmin[1];
  assign op3 = hexlightmin[2];
  assign op4 = consta;

  // Notes on the sheet:
  //   Start / Stop
  //   Reset
  //   Clock Started
endmodule

module stage4 (
  input  in_1
);

  wire and_1_out, and_2_out, and_3_out, and_4_out, button_1_out, button_2_out, not_1_out, or_1_out, or_2_out,
       stage1_1_output1, stage2_1_ouput1, stage3_1_output5;
  wire [3:0] j_k_ff_1_q, j_k_ff_2_q, stage2_1_hexlightsec, stage3_1_hexlightmin;

  Button button_1 (.out(button_1_out));
  Button button_2 (.out(button_2_out));
  J_K_Flip_Flop #(.trigger("falling")) j_k_ff_1 (
    .J(and_4_out), .K(and_4_out), .clk(stage3_1_output5), .Q(j_k_ff_1_q[0]), .reset(or_1_out));  // open: Qn, preset
  J_K_Flip_Flop #(.trigger("falling")) j_k_ff_2 (
    .J(and_4_out), .K(and_4_out), .clk(and_1_out), .Q(j_k_ff_2_q[0]), .preset(or_2_out));  // open: Qn, reset
  or or_1 (or_1_out, button_2_out, and_1_out);
  or or_2 (or_2_out, button_2_out, and_2_out);
  J_K_Flip_Flop #(.trigger("falling")) j_k_ff_3 (
    .J(and_4_out), .K(and_4_out), .clk(j_k_ff_1_q[0]), .Q(j_k_ff_1_q[1]), .preset(button_2_out),
    .reset(and_1_out));  // open: Qn
  J_K_Flip_Flop #(.trigger("falling")) j_k_ff_4 (
    .J(and_4_out), .K(and_4_out), .clk(j_k_ff_2_q[0]), .Q(j_k_ff_2_q[1]), .preset(or_2_out));  // open: Qn, reset
  LED led_1 (.in(stage1_1_output1));
  stage1 stage1_1 (.start(button_1_out), .reset(button_2_out), .output1(stage1_1_output1));
  stage2 stage2_1 (
    .start(stage1_1_output1), .reset(button_2_out), .hexlightsec(stage2_1_hexlightsec),
    .ouput1(stage2_1_ouput1));  // open: op1, op2, op3, op4
  stage3 stage3_1 (
    .start(stage1_1_output1), .reset(button_2_out), .sig(stage2_1_ouput1), .consta(in_1),
    .hexlightmin(stage3_1_hexlightmin), .output5(stage3_1_output5));  // open: op1, op2, op3, op4
  J_K_Flip_Flop #(.trigger("falling")) j_k_ff_5 (
    .J(and_4_out), .K(and_4_out), .clk(j_k_ff_1_q[1]), .Q(j_k_ff_1_q[2]), .preset(button_2_out),
    .reset(and_1_out));  // open: Qn
  J_K_Flip_Flop #(.trigger("falling")) j_k_ff_6 (
    .J(and_4_out), .K(and_4_out), .clk(j_k_ff_2_q[1]), .Q(j_k_ff_2_q[2]), .reset(or_2_out));  // open: Qn, preset
  J_K_Flip_Flop #(.trigger("falling")) j_k_ff_7 (
    .J(and_4_out), .K(and_4_out), .clk(j_k_ff_1_q[2]), .Q(j_k_ff_1_q[3]), .reset(or_1_out));  // open: Qn, preset
  and and_1 (and_1_out, j_k_ff_1_q[1], j_k_ff_1_q[3]);
  J_K_Flip_Flop #(.trigger("falling")) j_k_ff_8 (
    .J(and_4_out), .K(and_4_out), .clk(j_k_ff_2_q[2]), .Q(j_k_ff_2_q[3]), .reset(or_2_out));  // open: Qn, preset
  and and_2 (and_2_out, j_k_ff_2_q[1], j_k_ff_2_q[3]);
  Hex_Digit_Display hex_digit_display_1 (.value(j_k_ff_2_q));  // open: dp
  Hex_Digit_Display hex_digit_display_2 (.value(j_k_ff_1_q));  // open: dp
  Hex_Digit_Display hex_digit_display_3 (.value(stage2_1_hexlightsec));  // open: dp
  Hex_Digit_Display hex_digit_display_4 (.value(stage3_1_hexlightmin));  // open: dp
  and and_3 (and_3_out, j_k_ff_1_q[0], j_k_ff_1_q[3], j_k_ff_2_q[0], j_k_ff_2_q[3]);
  not not_1 (not_1_out, and_3_out);
  and and_4 (and_4_out, stage1_1_output1, not_1_out);

  // Notes on the sheet:
  //   Studentid: 106212636
  //   Start / Stop
  //   Reset
  //   :
endmodule
