// Logisim project stage5.circ as structural Verilog: 6 circuits, main circuit stage2
module stage1 (
  input  start,
  input  reset,
  output output1
);

  J_K_Flip_Flop j_k_ff_1 (.J(start), .K(start), .clk(start), .Q(output1), .reset(reset));  // open: Qn, preset
  LED led_1 (.in(output1));

  // Notes on the sheet:
  //   Start / Stop
  //   Reset
  //   Clock Started
  //   Sending signal to other stage
endmodule

module stage2 (
  input  start,
  input  reset,
  output op1,
  output op2,
  output op3,
  output op4,
  output [3:0] hexlightsec,
  output ouput5
);

  wire clock_1_out, or_1_out, stage1_1_output1;

  Clock clock_1 (.out(clock_1_out));
  J_K_Flip_Flop #(.trigger("falling")) j_k_ff_1 (
    .J(stage1_1_output1), .K(stage1_1_output1), .clk(clock_1_out), .Q(hexlightsec[0]), .reset(or_1_out));  // open: Qn, preset
  or or_1 (or_1_out, reset, ouput5);
  J_K_Flip_Flop #(.trigger("falling")) j_k_ff_2 (
    .J(stage1_1_output1), .K(stage1_1_output1), .clk(hexlightsec[0]), .Q(hexlightsec[1]), .reset(or_1_out));  // open: Qn, preset
  stage1 stage1_1 (.start(start), .reset(reset), .output1(stage1_1_output1));
  J_K_Flip_Flop #(.trigger("falling")) j_k_ff_3 (
    .J(stage1_1_output1), .K(stage1_1_output1), .clk(hexlightsec[1]), .Q(hexlightsec[2]), .reset(or_1_out));  // open: Qn, preset
  LED led_1 (.in(stage1_1_output1));
  J_K_Flip_Flop #(.trigger("falling")) j_k_ff_4 (
    .J(stage1_1_output1), .K(stage1_1_output1), .clk(hexlightsec[2]), .Q(hexlightsec[3]), .reset(or_1_out));  // open: Qn, preset
  and and_1 (ouput5, hexlightsec[1], hexlightsec[3]);

  assign op1 = hexlightsec[0];
  assign op2 = hexlightsec[1];
  assign op3 = hexlightsec[2];
  assign op4 = hexlightsec[3];

  // Notes on the sheet:
  //   Start / Stop
  //   Reset
  //   Clock Started
endmodule

module stage3 (
  input  start,
  input  reset,
  input  sig,
  input  consta,
  output [3:0] hexlightmin,
  output op1,
  output op2,
  output op3,
  output op4,
  output output5
);

  wire not_1_out, or_1_out, stage1_1_output1, stage2_1_op2, stage2_1_ouput5;
  wire [3:0] stage2_1_hexlightsec;

  stage1 stage1_1 (.start(start), .reset(reset), .output1(stage1_1_output1));
  J_K_Flip_Flop #(.trigger("falling")) j_k_ff_1 (
    .J(stage1_1_output1), .K(stage1_1_output1), .clk(sig), .Q(hexlightmin[0]), .reset(or_1_out));  // open: Qn, preset
  or or_1 (or_1_out, reset, output5);
  LED led_1 (.in(stage1_1_output1));
  not not_1 (not_1_out, hexlightmin[0]);
  J_K_Flip_Flop #(.trigger("falling")) j_k_ff_2 (
    .J(stage1_1_output1), .K(stage1_1_output1), .clk(hexlightmin[0]), .Q(hexlightmin[1]), .reset(or_1_out));  // open: Qn, preset
  and and_1 (output5, not_1_out, hexlightmin[1], hexlightmin[2]);
  stage2 stage2_1 (
    .start(stage1_1_output1), .reset(reset), .op2(stage2_1_op2), .hexlightsec(stage2_1_hexlightsec),
    .ouput5(stage2_1_ouput5));  // open: op1, op3, op4
  J_K_Flip_Flop #(.trigger("falling")) j_k_ff_3 (
    .J(stage1_1_output1), .K(stage1_1_output1), .clk(hexlightmin[1]), .Q(hexlightmin[2]), .reset(or_1_out));  // open: Qn, preset
  Hex_Digit_Display hex_digit_display_1 (.value(stage2_1_hexlightsec));  // open: dp

  assign hexlightmin[3] = consta;
  assign op1 = hexlightmin[0];
  assign op2 = hexlightmin[1];
  assign op3 = hexlightmin[2];
  assign op4 = consta;

  // Notes on the sheet:
  //   Start / Stop
  //   Reset
  //   Clock Started
endmodule

module stage4 (
  input  start,
  input  reset,
  input  sig,
  output op1,
  output op2,
  output op3,
  output op4,
  output [3:0] out_8,
  output op6,
  output op7,
  output op8,
  output op9,
  output [3:0] out_13
);

  wire and_1_out, and_2_out, or_1_out, or_2_out;

  J_K_Flip_Flop #(.trigger("falling")) j_k_ff_1 (
    .J(start), .K(start), .clk(sig), .Q(op1), .reset(or_1_out));  // open: Qn, preset
  J_K_Flip_Flop #(.trigger("falling")) j_k_ff_2 (
    .J(start), .K(start), .clk(and_1_out), .Q(op6), .preset(or_2_out));  // open: Qn, reset
  or or_1 (or_1_out, reset, and_1_out);
  or or_2 (or_2_out, reset, and_2_out);
  J_K_Flip_Flop #(.trigger("falling")) j_k_ff_3 (
    .J(start), .K(start), .clk(op1), .Q(op2), .preset(reset), .reset(and_1_out));  // open: Qn
  J_K_Flip_Flop #(.trigger("falling")) j_k_ff_4 (
    .J(start), .K(start), .clk(op6), .Q(op7), .preset(or_2_out));  // open: Qn, reset
  J_K_Flip_Flop #(.trigger("falling")) j_k_ff_5 (
    .J(start), .K(start), .clk(op2), .Q(op3), .preset(reset), .reset(and_1_out));  // open: Qn
  J_K_Flip_Flop #(.trigger("falling")) j_k_ff_6 (
    .J(start), .K(start), .clk(op7), .Q(op8), .reset(or_2_out));  // open: Qn, preset
  J_K_Flip_Flop #(.trigger("falling")) j_k_ff_7 (
    .J(start), .K(start), .clk(op3), .Q(op4), .reset(or_1_out));  // open: Qn, preset
  and and_1 (and_1_out, op2, op4);
  J_K_Flip_Flop #(.trigger("falling")) j_k_ff_8 (
    .J(start), .K(start), .clk(op8), .Q(op9), .reset(or_2_out));  // open: Qn, preset
  and and_2 (and_2_out, op7, op9);

  assign out_8 = {op4, op3, op2, op1};
  assign out_13 = {op9, op8, op7, op6};
endmodule

module stage5 (
  input  in_1,
  output [3:0] lighmin1,
  output [3:0] lightmin2,
  output [3:0] lighsec1,
  output [3:0] lighsec2
);

  wire button_1_out, button_2_out, button_3_out, split_counter_1_clock, stage1_1_output1, stage2_1_op1,
       stage2_1_op2, stage2_1_op3, stage2_1_op4, stage2_1_ouput5, stage3_1_op1, stage3_1_op2, stage3_1_op3,
       stage3_1_op4, stage3_1_output5, stage4_1_op1, stage4_1_op2, stage4_1_op3, stage4_1_op4, stage4_1_op6,
       stage4_1_op7, stage4_1_op8, stage4_1_op9;
  wire [3:0] stage2_1_hexlightsec, stage3_1_hexlightmin, stage4_1_out_8, stage4_1_out_13;

  Button button_1 (.out(button_1_out));
  Button button_2 (.out(button_2_out));
  stage1 stage1_1 (.start(button_1_out), .reset(button_2_out), .output1(stage1_1_output1));
  LED led_1 (.in(stage1_1_output1));
  stage2 stage2_1 (
    .start(stage1_1_output1), .reset(button_2_out), .op1(stage2_1_op1), .op2(stage2_1_op2),
    .op3(stage2_1_op3), .op4(stage2_1_op4), .hexlightsec(stage2_1_hexlightsec), .ouput5(stage2_1_ouput5));
  stage3 stage3_1 (
    .start(stage1_1_output1), .reset(button_2_out), .sig(stage2_1_ouput5), .consta(in_1),
    .hexlightmin(stage3_1_hexlightmin), .op1(stage3_1_op1), .op2(stage3_1_op2), .op3(stage3_1_op3),
    .op4(stage3_1_op4), .output5(stage3_1_output5));
  stage4 stage4_1 (
    .start(stage1_1_output1), .reset(button_2_out), .sig(stage3_1_output5), .op1(stage4_1_op1),
    .op2(stage4_1_op2), .op3(stage4_1_op3), .op4(stage4_1_op4), .out_8(stage4_1_out_8), .op6(stage4_1_op6),
    .op7(stage4_1_op7), .op8(stage4_1_op8), .op9(stage4_1_op9), .out_13(stage4_1_out_13));
  Hex_Digit_Display hex_digit_display_1 (.value(stage4_1_out_13));  // open: dp
  Hex_Digit_Display hex_digit_display_2 (.value(stage4_1_out_8));  // open: dp
  Hex_Digit_Display hex_digit_display_3 (.value(stage3_1_hexlightmin));  // open: dp
  Hex_Digit_Display hex_digit_display_4 (.value(stage2_1_hexlightsec));  // open: dp
  Button button_3 (.out(button_3_out));
  D_Flip_Flop d_ff_1 (
    .D(stage2_1_op1), .clk(split_counter_1_clock), .Q(lighsec2[0]), .reset(button_2_out));  // open: Qn, preset
  D_Flip_Flop d_ff_2 (
    .D(stage2_1_op2), .clk(split_counter_1_clock), .Q(lighsec2[1]), .reset(button_2_out));  // open: Qn, preset
  D_Flip_Flop d_ff_3 (
    .D(stage2_1_op3), .clk(split_counter_1_clock), .Q(lighsec2[2]), .reset(button_2_out));  // open: Qn, preset
  D_Flip_Flop d_ff_4 (
    .D(stage2_1_op4), .clk(split_counter_1_clock), .Q(lighsec2[3]), .reset(button_2_out));  // open: Qn, preset
  D_Flip_Flop d_ff_5 (
    .D(stage3_1_op1), .clk(split_counter_1_clock), .Q(lighsec1[0]), .reset(button_2_out));  // open: Qn, preset
  D_Flip_Flop d_ff_6 (
    .D(stage3_1_op2), .clk(split_counter_1_clock), .Q(lighsec1[1]), .reset(button_2_out));  // open: Qn, preset
  D_Flip_Flop d_ff_7 (
    .D(stage3_1_op3), .clk(split_counter_1_clock), .Q(lighsec1[2]), .reset(button_2_out));  // open: Qn, preset
  D_Flip_Flop d_ff_8 (
    .D(stage3_1_op4), .clk(split_counter_1_clock), .Q(lighsec1[3]), .reset(button_2_out));  // open: Qn, preset
  D_Flip_Flop d_ff_9 (
    .D(stage4_1_op1), .clk(split_counter_1_clock), .Q(lightmin2[0]), .reset(button_2_out));  // open: Qn, preset
  D_Flip_Flop d_ff_10 (
    .D(stage4_1_op2), .clk(split_counter_1_clock), .Q(lightmin2[1]), .preset(button_2_out));  // open: Qn, reset
  D_Flip_Flop d_ff_11 (
    .D(stage4_1_op3), .clk(split_counter_1_clock), .Q(lightmin2[2]), .preset(button_2_out));  // open: Qn, reset
  D_Flip_Flop d_ff_12 (
    .D(stage4_1_op4), .clk(split_counter_1_clock), .Q(lightmin2[3]), .reset(button_2_out));  // open: Qn, preset
  D_Flip_Flop d_ff_13 (
    .D(stage4_1_op6), .clk(split_counter_1_clock), .Q(lighmin1[0]), .preset(button_2_out));  // open: Qn, reset
  D_Flip_Flop d_ff_14 (
    .D(stage4_1_op7), .clk(split_counter_1_clock), .Q(lighmin1[1]), .preset(button_2_out));  // open: Qn, reset
  D_Flip_Flop d_ff_15 (
    .D(stage4_1_op8), .clk(split_counter_1_clock), .Q(lighmin1[2]), .reset(button_2_out));  // open: Qn, preset
  D_Flip_Flop d_ff_16 (
    .D(stage4_1_op9), .clk(split_counter_1_clock), .Q(lighmin1[3]), .reset(button_2_out));  // open: Qn, preset
  split_counter split_counter_1 (.split(button_3_out), .reset(button_2_out), .clock(split_counter_1_clock));
  Hex_Digit_Display hex_digit_display_5 (.value(lighmin1));  // open: dp
  Hex_Digit_Display hex_digit_display_6 (.value(lightmin2));  // open: dp
  Hex_Digit_Display hex_digit_display_7 (.value(lighsec1));  // open: dp
  Hex_Digit_Display hex_digit_display_8 (.value(lighsec2));  // open: dp

  // Notes on the sheet:
  //   start/stop
  //   reset
  //   studentid: 106212636
  //   Clock Started
  //   Minutes
  //   Elapsed Time
  //   Seconds
  //   :
  //   split
  //   Minutes
  //   Split Time
  //   :
  //   Seconds
endmodule

module split_counter (
  input  split,
  input  reset,
  output clock
);

  wire and_1_out, and_2_out, j_k_ff_1_q, j_k_ff_2_q, j_k_ff_3_q, not_1_out, not_2_out;

  and and_1 (and_1_out, not_1_out, 1'b1);
  not not_1 (not_1_out, and_2_out);
  J_K_Flip_Flop #(.trigger("falling")) j_k_ff_1 (
    .J(and_1_out), .K(and_1_out), .clk(split), .Q(j_k_ff_1_q), .reset(reset));  // open: Qn, preset
  J_K_Flip_Flop #(.trigger("falling")) j_k_ff_2 (
    .J(and_1_out), .K(and_1_out), .clk(j_k_ff_1_q), .Q(j_k_ff_2_q), .reset(reset));  // open: Qn, preset
  J_K_Flip_Flop #(.trigger("falling")) j_k_ff_3 (
    .J(and_1_out), .K(and_1_out), .clk(j_k_ff_2_q), .Q(j_k_ff_3_q), .reset(reset));  // open: Qn, preset
  and and_2 (and_2_out, j_k_ff_2_q, j_k_ff_3_q);
  not not_2 (not_2_out, and_2_out);
  and and_3 (clock, split, not_2_out);
endmodule
