// Logisim project Lab_week3.circ as structural Verilog: 1 circuit, main circuit main
module main (
  input  in_1,
  input  in_2,
  input  in_3,
  input  in_4,
  input  in_5,
  input  in_6,
  input  in_7,
  input  in_8,
  input  in_9,
  input  in_10,
  input  in_11,
  input  in_12,
  input  J,
  input  K
);

  wire and_1_out, and_2_out, and_3_out, and_4_out, and_5_out, and_6_out, and_7_out, and_8_out, clock_1_out,
       clock_2_out, clock_3_out, clock_4_out, clock_5_out, d_ff_1_q, d_ff_2_q, d_ff_3_q, d_ff_4_q, d_ff_5_q,
       d_ff_6_q, d_ff_7_q, d_ff_8_q, nand_1_out, nand_2_out, nor_1_out, nor_2_out, nor_3_out, nor_4_out,
       nor_5_out, nor_6_out, not_1_out, not_2_out;

  Clock clock_1 (.out(clock_1_out));
  Clock clock_2 (.out(clock_2_out));
  D_Flip_Flop d_ff_1 (.D(in_7), .clk(clock_2_out), .Q(d_ff_1_q), .reset(in_11));  // open: Qn, preset
  Clock clock_3 (.out(clock_3_out));
  LED led_1 (.in(d_ff_1_q));
  not not_1 (not_1_out, in_12);
  Clock clock_4 (.out(clock_4_out));
  Clock clock_5 (.out(clock_5_out));
  D_Flip_Flop d_ff_2 (.D(d_ff_4_q), .clk(clock_3_out), .Q(d_ff_2_q));  // open: Qn, preset, reset
  not not_2 (not_2_out, in_6);
  D_Flip_Flop d_ff_3 (.D(in_8), .clk(clock_2_out), .Q(d_ff_3_q), .reset(in_11));  // open: Qn, preset
  LED led_2 (.in(d_ff_2_q));
  nand nand_1 (nand_1_out, in_2, nand_2_out);
  nand nand_2 (nand_2_out, nand_1_out, in_3);
  nor nor_1 (nor_1_out, in_4, nor_2_out);
  nor nor_2 (nor_2_out, nor_1_out, in_5);
  and and_1 (and_1_out, clock_1_out, not_2_out);
  and and_2 (and_2_out, clock_1_out, in_6);
  LED led_3 (.in(d_ff_3_q));
  and and_3 (and_3_out, not_1_out, clock_4_out);
  and and_4 (and_4_out, clock_4_out, in_12);
  and and_5 (and_5_out, and_8_out, J, clock_5_out);
  and and_6 (and_6_out, clock_5_out, K, and_7_out);
  D_Flip_Flop d_ff_4 (.D(d_ff_6_q), .clk(clock_3_out), .Q(d_ff_4_q));  // open: Qn, preset, reset
  LED led_4 (.in(nor_1_out));
  LED led_5 (.in(nor_2_out));
  D_Flip_Flop d_ff_5 (.D(in_9), .clk(clock_2_out), .Q(d_ff_5_q), .reset(in_11));  // open: Qn, preset
  D_Flip_Flop d_ff_6 (.D(d_ff_8_q), .clk(clock_3_out), .Q(d_ff_6_q));  // open: Qn, preset, reset
  LED led_6 (.in(d_ff_4_q));
  LED led_7 (.in(nand_1_out));
  LED led_8 (.in(nand_2_out));
  nor nor_3 (nor_3_out, and_1_out, nor_4_out);
  nor nor_4 (nor_4_out, nor_3_out, and_2_out);
  D_Flip_Flop d_ff_7 (.D(in_10), .clk(clock_2_out), .Q(d_ff_7_q), .reset(in_11));  // open: Qn, preset
  LED led_9 (.in(d_ff_5_q));
  nor nor_5 (nor_5_out, and_3_out, nor_6_out);
  nor nor_6 (nor_6_out, nor_5_out, and_4_out);
  and and_7 (and_7_out, and_5_out, and_8_out);
  and and_8 (and_8_out, and_7_out, and_6_out);
  D_Flip_Flop d_ff_8 (.D(in_1), .clk(clock_3_out), .Q(d_ff_8_q));  // open: Qn, preset, reset
  LED led_10 (.in(d_ff_6_q));
  LED led_11 (.in(nor_3_out));
  LED led_12 (.in(nor_4_out));
  LED led_13 (.in(d_ff_7_q));
  LED led_14 (.in(nor_5_out));
  LED led_15 (.in(nor_6_out));
  LED led_16 (.in(and_7_out));
  LED led_17 (.in(and_8_out));
  LED led_18 (.in(d_ff_8_q));

  // Notes on the sheet:
  //   Clock
endmodule
