// Logisim project week4_lab.circ as structural Verilog: 1 circuit, main circuit main
module main (
  input  in_1,
  input  in_2,
  input  in_3,
  input  in_4,
  input  in_5
);

  wire and_1_out, and_2_out, and_3_out, and_4_out, and_5_out, clock_1_out, clock_2_out, clock_3_out,
       clock_4_out, j_k_ff_1_q, j_k_ff_2_q, j_k_ff_4_q, j_k_ff_5_q, j_k_ff_7_q, j_k_ff_8_q, j_k_ff_10_q,
       j_k_ff_11_q, j_k_ff_12_q, j_k_ff_13_q;
  wire [2:0] j_k_ff_3_q;

  Clock clock_1 (.out(clock_1_out));
  Clock clock_2 (.out(clock_2_out));
  J_K_Flip_Flop j_k_ff_1 (.J(in_2), .K(in_2), .clk(clock_1_out), .Q(j_k_ff_1_q), .reset(in_3));  // open: Qn, preset
  Clock clock_3 (.out(clock_3_out));
  J_K_Flip_Flop #(.trigger("falling")) j_k_ff_2 (
    .J(1'b1), .K(1'b1), .clk(clock_2_out), .Q(j_k_ff_2_q), .reset(and_1_out));  // open: Qn, preset
  LED led_1 (.in(j_k_ff_2_q));
  LED led_2 (.in(j_k_ff_1_q));
  J_K_Flip_Flop j_k_ff_3 (
    .J(in_4), .K(in_4), .clk(clock_3_out), .Q(j_k_ff_3_q[0]), .reset(and_3_out));  // open: Qn, preset
  and and_1 (and_1_out, j_k_ff_4_q, j_k_ff_10_q);
  J_K_Flip_Flop #(.trigger("falling")) j_k_ff_4 (
    .J(1'b1), .K(1'b1), .clk(j_k_ff_2_q), .Q(j_k_ff_4_q), .reset(and_1_out));  // open: Qn, preset
  J_K_Flip_Flop j_k_ff_5 (
    .J(j_k_ff_1_q), .K(j_k_ff_1_q), .clk(clock_1_out), .Q(j_k_ff_5_q), .reset(in_3));  // open: Qn, preset
  LED led_3 (.in(j_k_ff_3_q[0]));
  LED led_4 (.in(j_k_ff_4_q));
  LED led_5 (.in(j_k_ff_5_q));
  J_K_Flip_Flop j_k_ff_6 (
    .J(j_k_ff_3_q[0]), .K(j_k_ff_3_q[0]), .clk(clock_3_out), .Q(j_k_ff_3_q[1]), .reset(and_3_out));  // open: Qn, preset
  J_K_Flip_Flop #(.trigger("falling")) j_k_ff_7 (
    .J(1'b1), .K(1'b1), .clk(j_k_ff_4_q), .Q(j_k_ff_7_q), .reset(and_1_out));  // open: Qn, preset
  J_K_Flip_Flop j_k_ff_8 (
    .J(j_k_ff_5_q), .K(j_k_ff_5_q), .clk(clock_1_out), .Q(j_k_ff_8_q), .reset(in_3));  // open: Qn, preset
  and and_2 (and_2_out, j_k_ff_3_q[0], j_k_ff_3_q[1]);
  LED led_6 (.in(j_k_ff_3_q[1]));
  LED led_7 (.in(j_k_ff_7_q));
  LED led_8 (.in(j_k_ff_8_q));
  J_K_Flip_Flop j_k_ff_9 (
    .J(and_2_out), .K(and_2_out), .clk(clock_3_out), .Q(j_k_ff_3_q[2]), .reset(and_3_out));  // open: Qn, preset
  LED led_9 (.in(j_k_ff_3_q[2]));
  J_K_Flip_Flop #(.trigger("falling")) j_k_ff_10 (
    .J(1'b1), .K(1'b1), .clk(j_k_ff_7_q), .Q(j_k_ff_10_q), .reset(and_1_out));  // open: Qn, preset
  LED led_10 (.in(j_k_ff_10_q));
  and and_3 (and_3_out, j_k_ff_3_q[1], j_k_ff_3_q[2]);
  Hex_Digit_Display hex_digit_display_1 (.value({in_5, j_k_ff_3_q}));  // open: dp
  Clock clock_4 (.out(clock_4_out));
  J_K_Flip_Flop j_k_ff_11 (
    .J(in_1), .K(in_1), .clk(clock_4_out), .Q(j_k_ff_11_q), .reset(and_5_out));  // open: Qn, preset
  LED led_11 (.in(j_k_ff_11_q));
  J_K_Flip_Flop j_k_ff_12 (
    .J(j_k_ff_11_q), .K(j_k_ff_11_q), .clk(clock_4_out), .Q(j_k_ff_12_q), .reset(and_5_out));  // open: Qn, preset
  LED led_12 (.in(j_k_ff_12_q));
  and and_4 (and_4_out, j_k_ff_11_q, j_k_ff_12_q);
  J_K_Flip_Flop j_k_ff_13 (
    .J(and_4_out), .K(and_4_out), .clk(clock_4_out), .Q(j_k_ff_13_q), .reset(and_5_out));  // open: Qn, preset
  LED led_13 (.in(j_k_ff_13_q));
  and and_5 (and_5_out, j_k_ff_12_q, j_k_ff_13_q);
endmodule
