// Logisim project week5_lab.circ as structural Verilog: 1 circuit, main circuit main
module main (
  input  in_1,
  input  in_2,
  input  in_3,
  input  in_4,
  input  in_5,
  input  in_6,
  input  in_7,
  input  in_8,
  input  in_9,
  input  in_10,
  input  in_11,
  input  in_12
);

  wire and_1_out, and_2_out, and_3_out, and_4_out, and_5_out, and_6_out, and_7_out, and_8_out, and_9_out,
       and_10_out, and_11_out, and_12_out, and_13_out, and_14_out, and_15_out, and_16_out, and_17_out,
       and_18_out, and_19_out, and_20_out, and_21_out, and_22_out, and_23_out, and_24_out, and_25_out,
       and_26_out, and_27_out, and_28_out, and_29_out, and_30_out, button_1_out, clock_1_out, clock_2_out,
       clock_3_out, d_ff_1_q, d_ff_2_q, d_ff_3_q, d_ff_4_q, d_ff_5_q, d_ff_6_q, d_ff_7_q, d_ff_8_q, d_ff_9_q,
       d_ff_10_q, d_ff_11_q, d_ff_12_q, not_1_out, not_2_out, not_3_out, not_4_out, or_1_out, or_2_out,
       or_3_out, or_4_out, or_5_out, or_6_out, or_7_out, or_8_out, or_9_out, or_10_out, or_11_out, or_12_out;

  Button button_1 (.out(button_1_out));
  Clock clock_1 (.out(clock_1_out));
  Clock clock_2 (.out(clock_2_out));
  Clock clock_3 (.out(clock_3_out));
  not not_1 (not_1_out, in_4);
  not not_2 (not_2_out, in_8);
  not not_3 (not_3_out, in_12);
  not not_4 (not_4_out, in_2);
  and and_1 (and_1_out, in_3, in_2);
  or or_1 (or_1_out, and_1_out, and_3_out);
  and and_2 (and_2_out, clock_2_out, not_3_out);
  and and_3 (and_3_out, not_4_out, d_ff_4_q);
  D_Flip_Flop d_ff_1 (.D(or_1_out), .clk(clock_3_out), .Q(d_ff_1_q), .reset(button_1_out));  // open: Qn, preset
  and and_4 (and_4_out, d_ff_6_q, not_1_out);
  and and_5 (and_5_out, in_4, in_6);
  and and_6 (and_6_out, d_ff_5_q, not_2_out);
  and and_7 (and_7_out, in_8, in_10);
  LED led_1 (.in(d_ff_1_q));
  or or_2 (or_2_out, and_4_out, and_5_out);
  D_Flip_Flop d_ff_2 (.D(or_2_out), .clk(clock_1_out), .Q(d_ff_2_q), .reset(in_7));  // open: Qn, preset
  or or_3 (or_3_out, and_6_out, and_7_out);
  D_Flip_Flop d_ff_3 (.D(or_3_out), .clk(and_2_out), .Q(d_ff_3_q), .reset(in_11));  // open: Qn, preset
  LED led_2 (.in(d_ff_2_q));
  and and_8 (and_8_out, d_ff_1_q, in_2);
  or or_4 (or_4_out, and_8_out, and_12_out);
  and and_9 (and_9_out, d_ff_8_q, not_2_out);
  and and_10 (and_10_out, in_8, d_ff_3_q);
  and and_11 (and_11_out, d_ff_3_q, not_3_out);
  LED led_3 (.in(and_11_out));
  and and_12 (and_12_out, not_4_out, in_1);
  and and_13 (and_13_out, d_ff_7_q, not_1_out);
  and and_14 (and_14_out, in_4, d_ff_2_q);
  D_Flip_Flop d_ff_4 (.D(or_4_out), .clk(clock_3_out), .Q(d_ff_4_q), .reset(button_1_out));  // open: Qn, preset
  or or_5 (or_5_out, and_13_out, and_14_out);
  or or_6 (or_6_out, and_9_out, and_10_out);
  D_Flip_Flop d_ff_5 (.D(or_6_out), .clk(and_2_out), .Q(d_ff_5_q), .reset(in_11));  // open: Qn, preset
  LED led_4 (.in(d_ff_4_q));
  D_Flip_Flop d_ff_6 (.D(or_5_out), .clk(clock_1_out), .Q(d_ff_6_q), .reset(in_7));  // open: Qn, preset
  LED led_5 (.in(d_ff_6_q));
  and and_15 (and_15_out, d_ff_5_q, not_3_out);
  and and_16 (and_16_out, d_ff_9_q, not_1_out);
  and and_17 (and_17_out, in_4, d_ff_6_q);
  and and_18 (and_18_out, d_ff_10_q, not_2_out);
  and and_19 (and_19_out, in_8, d_ff_5_q);
  LED led_6 (.in(and_15_out));
  or or_7 (or_7_out, and_18_out, and_19_out);
  or or_8 (or_8_out, and_16_out, and_17_out);
  D_Flip_Flop d_ff_7 (.D(or_8_out), .clk(clock_1_out), .Q(d_ff_7_q), .reset(in_7));  // open: Qn, preset
  D_Flip_Flop d_ff_8 (.D(or_7_out), .clk(and_2_out), .Q(d_ff_8_q), .reset(in_11));  // open: Qn, preset
  LED led_7 (.in(d_ff_7_q));
  and and_20 (and_20_out, d_ff_8_q, not_3_out);
  and and_21 (and_21_out, d_ff_11_q, not_1_out);
  and and_22 (and_22_out, in_4, d_ff_7_q);
  and and_23 (and_23_out, d_ff_12_q, not_2_out);
  and and_24 (and_24_out, in_8, d_ff_8_q);
  LED led_8 (.in(and_20_out));
  or or_9 (or_9_out, and_21_out, and_22_out);
  or or_10 (or_10_out, and_23_out, and_24_out);
  D_Flip_Flop d_ff_9 (.D(or_9_out), .clk(clock_1_out), .Q(d_ff_9_q), .reset(in_7));  // open: Qn, preset
  D_Flip_Flop d_ff_10 (.D(or_10_out), .clk(and_2_out), .Q(d_ff_10_q), .reset(in_11));  // open: Qn, preset
  LED led_9 (.in(d_ff_9_q));
  and and_25 (and_25_out, d_ff_10_q, not_3_out);
  LED led_10 (.in(and_25_out));
  and and_26 (and_26_out, in_5, not_1_out);
  and and_27 (and_27_out, in_4, d_ff_9_q);
  and and_28 (and_28_out, in_9, not_2_out);
  and and_29 (and_29_out, in_8, d_ff_10_q);
  or or_11 (or_11_out, and_26_out, and_27_out);
  or or_12 (or_12_out, and_28_out, and_29_out);
  D_Flip_Flop d_ff_11 (.D(or_11_out), .clk(clock_1_out), .Q(d_ff_11_q), .reset(in_7));  // open: Qn, preset
  D_Flip_Flop d_ff_12 (.D(or_12_out), .clk(and_2_out), .Q(d_ff_12_q), .reset(in_11));  // open: Qn, preset
  LED led_11 (.in(d_ff_11_q));
  and and_30 (and_30_out, d_ff_12_q, not_3_out);
  LED led_12 (.in(and_30_out));
endmodule
