// Logisim project Lab01.circ as structural Verilog: 1 circuit, main circuit main
module main (
  input  A,
  input  B,
  input  in_3,
  input  in_4,
  input  in_5,
  input  in_6,
  input  in_7,
  input  in_8,
  input  in_9,
  input  in_10
);

  wire and_1_out, and_2_out, and_3_out, and_4_out, and_5_out, and_6_out, not_1_out, not_2_out, not_3_out,
       not_4_out, not_5_out, not_6_out, or_1_out, or_2_out, or_3_out, xor_1_out;

  and and_1 (and_1_out, in_3, in_4);
  or or_1 (or_1_out, in_3, in_4);
  not not_1 (not_1_out, in_8);
  and and_2 (and_2_out, in_9, in_10);
  LED led_1 (.in(and_1_out));
  LED led_2 (.in(or_1_out));
  xor xor_1 (xor_1_out, in_3, in_4);
  LED led_3 (.in(xor_1_out));
  LED led_4 (.in(not_1_out));
  LED led_5 (.in(and_2_out));
  not not_2 (not_2_out, A);
  not not_3 (not_3_out, B);
  not not_4 (not_4_out, in_5);
  not not_5 (not_5_out, in_6);
  not not_6 (not_6_out, in_7);
  and and_3 (and_3_out, A, B);
  and and_4 (and_4_out, not_2_out, not_3_out);
  and and_5 (and_5_out, in_5, in_6, in_7);
  and and_6 (and_6_out, not_4_out, not_5_out, not_6_out);
  or or_2 (or_2_out, and_3_out, and_4_out);
  LED led_6 (.in(or_2_out));
  or or_3 (or_3_out, and_5_out, and_6_out);
  LED led_7 (.in(or_3_out));
endmodule
