// Logisim project lab2.circ as structural Verilog: 1 circuit, main circuit main
module main (
  input  in_1,
  input  in_2,
  input  in_3,
  input  in_4,
  input  in_5,
  input  Data0,
  input  Data1,
  input  Q,
  input  Data2,
  input  Data3,
  input  in_11,
  input  in_12,
  input  in_13,
  input  in_14,
  input  in_15,
  input  in_16,
  input  Data0_2,
  input  Data1_2,
  input  Data2_2,
  input  Data3_2,
  input  Data4,
  input  Data5,
  input  Data6,
  input  Data7
);

  wire and_1_out, and_2_out, and_3_out, and_4_out, and_5_out, and_6_out, and_7_out, and_8_out, and_9_out,
       and_10_out, and_11_out, and_12_out, and_13_out, and_14_out, and_15_out, and_16_out, and_17_out,
       and_18_out, and_19_out, and_20_out, and_21_out, and_22_out, and_23_out, and_24_out, and_25_out,
       and_26_out, and_27_out, and_28_out, and_29_out, and_30_out, and_31_out, and_32_out, and_33_out,
       and_34_out, not_1_out, not_2_out, not_3_out, not_4_out, not_5_out, not_6_out, not_7_out, not_8_out,
       not_9_out, not_10_out, not_11_out, not_12_out, not_13_out, not_14_out, not_15_out, not_16_out,
       not_17_out, not_18_out, not_19_out, not_20_out, not_21_out, not_22_out, not_23_out, not_24_out,
       not_25_out, not_26_out, not_27_out, not_28_out, not_29_out, or_1_out, or_2_out, or_3_out;

  not not_1 (not_1_out, in_2);
  not not_2 (not_2_out, in_5);
  not not_3 (not_3_out, in_4);
  not not_4 (not_4_out, in_4);
  not not_5 (not_5_out, in_5);
  not not_6 (not_6_out, in_13);
  not not_7 (not_7_out, in_11);
  not not_8 (not_8_out, in_12);
  not not_9 (not_9_out, in_11);
  not not_10 (not_10_out, in_12);
  not not_11 (not_11_out, in_13);
  not not_12 (not_12_out, in_11);
  not not_13 (not_13_out, in_11);
  not not_14 (not_14_out, in_13);
  not not_15 (not_15_out, in_12);
  not not_16 (not_16_out, in_12);
  not not_17 (not_17_out, in_13);
  and and_1 (and_1_out, in_1, in_2);
  and and_2 (and_2_out, not_1_out, in_3);
  and and_3 (and_3_out, not_2_out, not_3_out);
  and and_4 (and_4_out, in_5, not_4_out);
  and and_5 (and_5_out, not_5_out, in_4);
  and and_6 (and_6_out, in_5, in_4);
  and and_7 (and_7_out, not_6_out, not_7_out, not_8_out);
  and and_8 (and_8_out, in_13, not_9_out, not_10_out);
  and and_9 (and_9_out, not_11_out, in_12, not_12_out);
  and and_10 (and_10_out, in_13, in_12, not_13_out);
  and and_11 (and_11_out, not_14_out, not_15_out, in_11);
  and and_12 (and_12_out, in_13, not_16_out, in_11);
  and and_13 (and_13_out, not_17_out, in_12, in_11);
  and and_14 (and_14_out, in_13, in_12, in_11);
  and and_15 (and_15_out, Data0, and_3_out);
  and and_16 (and_16_out, Data1, and_4_out);
  and and_17 (and_17_out, Data2, and_5_out);
  and and_18 (and_18_out, Data3, and_6_out);
  and and_19 (and_19_out, Data0_2, and_7_out);
  and and_20 (and_20_out, Data1_2, and_8_out);
  and and_21 (and_21_out, Data2_2, and_9_out);
  and and_22 (and_22_out, Data3_2, and_10_out);
  and and_23 (and_23_out, Data4, and_11_out);
  and and_24 (and_24_out, Data5, and_12_out);
  and and_25 (and_25_out, Data6, and_13_out);
  and and_26 (and_26_out, Data7, and_14_out);
  or or_1 (or_1_out, and_1_out, and_2_out);
  LED led_1 (.in(or_1_out));
  or or_2 (or_2_out, and_15_out, and_16_out, and_17_out, and_18_out);
  LED led_2 (.in(or_2_out));
  or or_3 (or_3_out, and_19_out, and_20_out, and_21_out, and_22_out, and_23_out, and_24_out, and_25_out, and_26_out);
  not not_18 (not_18_out, in_16);
  not not_19 (not_19_out, in_15);
  not not_20 (not_20_out, in_14);
  not not_21 (not_21_out, in_15);
  not not_22 (not_22_out, in_14);
  not not_23 (not_23_out, in_16);
  not not_24 (not_24_out, in_14);
  not not_25 (not_25_out, in_14);
  not not_26 (not_26_out, in_16);
  not not_27 (not_27_out, in_15);
  not not_28 (not_28_out, in_15);
  not not_29 (not_29_out, in_16);
  and and_27 (and_27_out, or_3_out, not_18_out, not_19_out, not_20_out);
  and and_28 (and_28_out, or_3_out, in_16, not_21_out, not_22_out);
  and and_29 (and_29_out, or_3_out, not_23_out, in_15, not_24_out);
  and and_30 (and_30_out, or_3_out, in_16, in_15, not_25_out);
  and and_31 (and_31_out, or_3_out, not_26_out, not_27_out, in_14);
  and and_32 (and_32_out, or_3_out, in_16, not_28_out, in_14);
  and and_33 (and_33_out, or_3_out, not_29_out, in_15, in_14);
  and and_34 (and_34_out, or_3_out, in_16, in_15, in_14);
  LED led_3 (.in(and_27_out));
  LED led_4 (.in(and_28_out));
  LED led_5 (.in(and_29_out));
  LED led_6 (.in(and_30_out));
  LED led_7 (.in(and_31_out));
  LED led_8 (.in(and_32_out));
  LED led_9 (.in(and_33_out));
  LED led_10 (.in(and_34_out));

  // Notes on the sheet:
  //   Output0
  //   Output1
  //   Output2
  //   Output3
  //   Output4
  //   Output5
  //   Output6
  //   Output7
endmodule
